# Fritzing sketch DomusGuard (saved by Fritzing 0.9.2b)
circuit board: 8.47cm x 5.64cm
breadboards: 2

parts:
  Raspberry_Pi1 = Raspberry Pi 2
  Arduino_NRF = Arduino Pro Mini v13
  J4 = shrouded pin header, 8 pins [form="♂ (shrouded male)"]
  NRF = NRF24L01
  J3 = double row female pin header, 8 pins [form="♀ (female)"]
  Arduino_433 = Arduino Pro Mini v13
  U1 = RF-LINK_RX [package=rf-link_rx]
  U2 = RF-LINK_TX [package=rf-link_tx]
  Componente1 = Logic Level Converter

nets:
  N1: Raspberry_Pi1.3v3, J3.pin2
  N2: Raspberry_Pi1.GPIO2, J3.pin3
  N3: Raspberry_Pi1.GPIO3, J3.pin4
  N4: Raspberry_Pi1.GND, J3.pin1
  N5: Raspberry_Pi1.5V, J3.pin8
  5V: Arduino_NRF.VCC, J4.pin8, Componente1.HV
  GND: Arduino_NRF.GND, J4.pin1, NRF.GND, Arduino_433.GND, U1.GND, U2.GND, Componente1.GND
  N6: Arduino_NRF.A4, J4.pin3
  N7: Arduino_NRF.A5, J4.pin4
  N8: Arduino_NRF.D13/SCK, NRF.SCK
  N9: Arduino_NRF.D12/MISO, NRF.MISO
  N10: Arduino_NRF.D11_PWM/MOSI, NRF.MOSI
  N11: Arduino_NRF.D10_PWM/SS, NRF.CSN
  N12: Arduino_NRF.D8, NRF.CE
  N13: Arduino_NRF.D2, NRF.IRQ
  3.3V: J4.pin2, NRF.VCC, Arduino_433.VCC, Componente1.LV
  N14: Arduino_433.A4, Componente1.TX_LV
  N15: Arduino_433.A5, Componente1.RX_LV
  N16: Arduino_433.D10_PWM/SS, U2.DATA
  N17: Arduino_433.D2, U1.Data
  VCC: U1.VCC, U2.+5V

custom parts:
  RF-LINK_RX: RF Link receivers- WRL-8947, 8948, 8949, 8950
  RF-LINK_TX: Common RF transmitter of the 315.00Mhz varity
